# Fritzing sketch fritz (saved by Fritzing 0.9.10b)
breadboards: 1

parts:
  Mod1 = Amica NodeMCU DEVKIT 1.0
  Parça2 = NRF24L01
  U1 = TRANSISTOR_NPN_2 [package=to-92]
  U2 = TRANSISTOR_NPN_2 [package=to-92]
  U3 = TRANSISTOR_NPN_2 [package=to-92]
  U4 = TRANSISTOR_NPN_2 [package=to-92]
  R2 = Resistor [tolerance=±5% power=0.25 resistance=260 package=THT]  # not connected
  R3 = Resistor [tolerance=±5% power=0.25 resistance=220 package=THT]
  R4 = Resistor [tolerance=±5% power=0.25 resistance=220 package=THT]  # not connected
  R5 = Resistor [tolerance=±5% power=0.25 resistance=220 package=THT]
  LED2 = LED - 5mm [color="Red (633nm)" current=0.030 package="5 mm [THT]"]
  VCC1 = Battery block 9V
  Mod3 = Amica NodeMCU DEVKIT 1.0
  Parça4 = NRF24L01
  LED3 = LED - 5mm [color="Red (633nm)" current=0.030 package="5 mm [THT]"]
  LED4 = LED - 5mm [color="Red (633nm)" current=0.030 package="5 mm [THT]"]
  LED5 = LED - 5mm [color="Red (633nm)" current=0.030 package="5 mm [THT]"]

nets:
  N1: Mod1.pin1, Parça2.VCC
  N2: Mod1.pin2, Parça2.GND
  N3: Mod1.pin5, U1.B
  N4: Mod1.pin6, Parça2.MOSI
  N5: Mod1.pin7, Parça2.MISO
  N6: Mod1.pin8, Parça2.SCK
  N7: Mod1.pin_11, Parça2.CE
  N8: Mod1.pin_12, U4.B
  N9: Mod1.pin_13, Parça2.CSN
  N10: Mod1.pin_14, U2.B
  N11: Mod1.pin_15, U3.B
  N12: U1.C, LED2.cathode
  N13: U2.C, LED4.cathode
  N14: U3.C, LED5.cathode
  N15: U3.E, VCC1.-
  N16: U4.C, LED3.cathode
  N17: R3.Pin_0, R5.Pin_0, VCC1.+
  N18: R3.Pin_1, LED3.anode
  N19: R5.Pin_1, LED2.anode
  N20: Mod3.pin1, Parça4.VCC
  N21: Mod3.pin2, Mod3.pin3, Parça4.GND
  N22: Mod3.pin6, Parça4.MOSI
  N23: Mod3.pin7, Parça4.MISO
  N24: Mod3.pin8, Parça4.SCK
  N25: Mod3.pin_11, Parça4.CE
  N26: Mod3.pin_13, Parça4.CSN

// code stored in the sketch: Untitled.ino
/*AL?C?
#include <ESP8266WiFi.h>
#include <SPI.h>
#include <nRF24L01.h>
#include <RF24.h>
#define led1 D1
#define led3 D0
#define led4 D3
#define led2 D8


int buttonState = 0;


RF24 radio(D4,D2); // CE, CSN
const byte address[6] = "00002";


void setup() {
  Serial.begin(9600);
  pinMode(led1, OUTPUT);
  pinMode(led2, OUTPUT);  
  pinMode(led3, OUTPUT);
  pinMode(led4, OUTPUT);
  digitalWrite(led1, HIGH);
  digitalWrite(led2, HIGH);  
  digitalWrite(led3, HIGH);
  digitalWrite(led4, HIGH);
  radio.begin();
  radio.openReadingPipe(0, address);
  radio.setPALevel(RF24_PA_MIN);
}
void loop() {
  radio.startListening();
  while (!radio.available());
  radio.read(&buttonState, sizeof(buttonState));
  Serial.println(buttonState);


  if (buttonState == 1) {
    digitalWrite(led1, LOW);
  }
  else  if (buttonState == 0) {
    digitalWrite(led1, HIGH);
  }
  else if (buttonState == 3) {
    digitalWrite(led2, LOW);
  }
  else  if (buttonState == 2) {
    digitalWrite(led2, HIGH);
  }
  else  if (buttonState == 5) {
    digitalWrite(led3, LOW);
  }
  else  if (buttonState == 4) {
    digitalWrite(led3, HIGH);
  }  else  if (buttonState == 7) {
    digitalWrite(led4, LOW);
  }
  else  if (buttonState == 6) {
    digitalWrite(led4, HIGH);
  }
}

*/
/*
//verici
#define BLYNK_PRINT Serial
#include <ESP8266WiFi.h>
#include <SPI.h>
#include <nRF24L01.h>
#include <RF24.h>
#include <BlynkSimpleEsp8266.h>
#define BLYNK_AUTH_TOKEN "5_aIAECSRfCyr1iu1x5QeJU-5GbrTyVA"
char auth[] = BLYNK_AUTH_TOKEN;
char ssid[] = "EV"; //internet ad?n?z? yaz?n       MAD?S=FiberHGW_ZTGP2S_2.4GHz
char pass[] = "mustafa1969"; //internet ?ifrenizi yaz?n   MAD?S=43j7XPR7CK
int deger =0;
int deger1=0;
int deger2=0;
int deger3=0;


BLYNK_WRITE(V0){
    int pinValue = param.asInt();
    deger= param.asInt();
      analogWrite(D0,param.asInt());
      Serial.print("V0 Slider");
      Serial.println(pinValue);
}
BLYNK_WRITE(V1){
    int pinValue = param.asInt();
    deger1= param.asInt();
      analogWrite(D1,param.asInt());
      Serial.print("V0 Slider");
      Serial.println(pinValue);
}
BLYNK_WRITE(V2){
    int pinValue = param.asInt();
    deger2= param.asInt();
      analogWrite(D1,param.asInt());
      Serial.print("V0 Slider");
      Serial.println(pinValue);
}
BLYNK_WRITE(V3){
    int pinValue = param.asInt();
    deger3= param.asInt();
      analogWrite(D1,param.asInt());
      Serial.print("V0 Slider");
      Serial.println(pinValue);
}


#define buttonPin1 D1
#define buttonPin2 D3


int buttonState1 = 0;
int buttonState2 = 0;
int buttonState3 = 0;
int buttonState4 = 0;


RF24 radio(D4,D2); // CE, CSN


const byte address[6] = "00002";


void setup() {
  pinMode(buttonPin1, INPUT_PULLUP);
  pinMode(buttonPin2, INPUT_PULLUP);
  Serial.begin(9600);
  radio.begin();
  radio.openWritingPipe(address);
  radio.setPALevel(RF24_PA_MIN);
  radio.stopListening();
      Blynk.begin (auth, ssid, pass, "blynk.cloud", 80);
}
void loop() {
  buttonState1 = digitalRead(buttonPin1);
  buttonState2 = digitalRead(buttonPin2);
  buttonState1=deger;
  buttonState2=deger1;
  buttonState3=deger2;
  buttonState4=deger3;
  
  if (buttonState1 == 1)
  {
    buttonState1 = 1;
  }
  else  if (buttonState1 == 0)
  {
    buttonState1 = 0;
  }
  if (buttonState2 == 1)
  {
    buttonState2 = 3;
  }
  else  if (buttonState2 == 0)
  {
    buttonState2 = 2;
  }
    if (buttonState3 == 1)
  {
    buttonState3 = 5;
  }
  else  if (buttonState3 == 0)
  {
    buttonState3 = 4;
  }
   if (buttonState4 == 1)
  {
    buttonState4 = 7;
  }
  else  if (buttonState4 == 0)
  {
    buttonState4 = 6;
  }
  
  Serial.print(buttonState1);
  Serial.print("\t");
  Serial.print(buttonState2);
  Serial.print("\t");
  Serial.print(buttonState3);
  Serial.print("\t");
  Serial.println(buttonState4);
  radio.write(&buttonState1, sizeof(buttonState1));
  radio.write(&buttonState2, sizeof(buttonState2));
  radio.write(&buttonState3, sizeof(buttonState3));
  radio.write(&buttonState4, sizeof(buttonState4));
    Blynk.run(); 
}*/
